// Digital circuit Instruction-decoder.dig as structural Verilog
module Instruction_decoder (
  input  [31:0] PC_In,
  output beq,
  output bge,
  output bgeu,
  output blt,
  output bltu,
  output bne,
  output addi,
  output andi,
  output csrrc,
  output csrrci,
  output csrrs,
  output csrrsi,
  output csrrw,
  output csrrwi,
  output [2:0] ebreak,
  output [2:0] ecall,
  output [2:0] jalr,
  output lb,
  output lbu,
  output ld,
  output lh,
  output lhu,
  output lw,
  output ori,
  output slli,
  output slti,
  output sltiu,
  output srai,
  output srli,
  output xori,
  output [2:0] jal,
  output add,
  output \and ,
  output [2:0] mret,
  output \or ,
  output [2:0] sfence_vma,
  output sll,
  output slt,
  output sltu,
  output sra,
  output [2:0] sret,
  output srl,
  output sub,
  output [2:0] wfi,
  output \xor ,
  output sb,
  output sh,
  output sw,
  output auipc,
  output lui,
  output fence,
  output fence_i
);

  wire and_1_out, and_2_out, and_3_out, and_4_out, and_5_out, demultiplexer_1_out_0, demultiplexer_1_out_1,
       demultiplexer_1_out_2, demultiplexer_1_out_3, demultiplexer_1_out_4, demultiplexer_1_out_5,
       demultiplexer_1_out_6, demultiplexer_4_out_3, nor_1_out, xor_1_out;
  wire [2:0] demultiplexer_5_out_0, driver_2_out, driver_3_out, driver_4_out, driver_5_out;
  wire [2:1] op;
  wire [3:0] lookuptable_1_out;

  LookUpTable #(.Bits(3)) lookuptable_1 (
    .in0(PC_In[0]), .in1(PC_In[1]), .in2(PC_In[2]), .in3(PC_In[3]), .in4(PC_In[4]), .in5(PC_In[5]),
    .in6(PC_In[6]), .out(lookuptable_1_out[2:0]));
  Demultiplexer #(.Selector_Bits(4)) demultiplexer_1 (
    .sel(lookuptable_1_out), .in(1'b1), .out_0(demultiplexer_1_out_0), .out_1(demultiplexer_1_out_1),
    .out_2(demultiplexer_1_out_2), .out_3(demultiplexer_1_out_3), .out_4(demultiplexer_1_out_4),
    .out_5(demultiplexer_1_out_5), .out_6(demultiplexer_1_out_6));  // open: out_7, out_8, out_9, out_10, out_11, out_12, out_13, out_14, out_15
  assign jal = demultiplexer_1_out_6 ? {op, 1'b1} : 3'bz;  // Driver driver_1
  assign driver_2_out = demultiplexer_1_out_5 ? PC_In[14:12] : 3'bz;  // Driver driver_2
  assign driver_3_out = demultiplexer_1_out_1 ? PC_In[14:12] : 3'bz;  // Driver driver_3
  assign driver_4_out = demultiplexer_1_out_2 ? PC_In[14:12] : 3'bz;  // Driver driver_4
  assign driver_5_out = demultiplexer_1_out_3 ? PC_In[14:12] : 3'bz;  // Driver driver_5
  Demultiplexer #(.Selector_Bits(3)) demultiplexer_2 (
    .sel(driver_2_out), .in(1'b1), .out_0(lb), .out_1(lh), .out_2(lw), .out_3(ld), .out_4(lbu), .out_5(lhu),
    .out_6(demultiplexer_1_out_0), .out_7(demultiplexer_1_out_0));
  Demultiplexer #(.Selector_Bits(3)) demultiplexer_3 (
    .sel(driver_3_out), .in(1'b1), .out_0(beq), .out_1(bne), .out_2(demultiplexer_1_out_0),
    .out_3(demultiplexer_1_out_0), .out_4(blt), .out_5(bge), .out_6(bltu), .out_7(bgeu));
  Demultiplexer #(.Selector_Bits(3)) demultiplexer_4 (
    .sel(driver_4_out), .in(1'b1), .out_0(addi), .out_1(slli), .out_2(slti), .out_3(demultiplexer_4_out_3),
    .out_4(xori), .out_5(sltiu), .out_6(ori), .out_7(andi));
  Demultiplexer #(.Selector_Bits(3)) demultiplexer_5 (
    .sel(driver_5_out), .in(1'b1), .out_0(demultiplexer_5_out_0[0]), .out_1(csrrw), .out_2(csrrs),
    .out_3(csrrc), .out_4(demultiplexer_1_out_0), .out_5(csrrwi), .out_6(csrrsi), .out_7(csrrci));
  nor nor_1 (nor_1_out, PC_In[25], PC_In[26], PC_In[27], PC_In[28], PC_In[29], PC_In[30], PC_In[31], PC_In[21], PC_In[22], PC_In[23], PC_In[24]);
  and and_1 (and_1_out, PC_In[21], PC_In[28], PC_In[29]);
  and and_2 (and_2_out, PC_In[25], PC_In[28]);
  and and_3 (and_3_out, PC_In[21], PC_In[28]);
  and and_4 (and_4_out, PC_In[20], PC_In[22], PC_In[28]);
  and and_5 (and_5_out, nor_1_out, PC_In[20]);
  xor xor_1 (xor_1_out, nor_1_out, PC_In[20]);
  assign jalr = demultiplexer_1_out_4 ? {op, 1'b1} : 3'bz;  // Driver driver_6
  // RelayDT relaydt_1: pin names not known; wires that end beside it: PC_In[30], demultiplexer_4_out_3, 1'b0, srai, srli
  assign ebreak = and_5_out ? demultiplexer_5_out_0 : 3'bz;  // Driver driver_7
  assign ecall = xor_1_out ? demultiplexer_5_out_0 : 3'bz;  // Driver driver_8
  assign mret = and_1_out ? demultiplexer_5_out_0 : 3'bz;  // Driver driver_9
  assign sfence_vma = and_2_out ? demultiplexer_5_out_0 : 3'bz;  // Driver driver_10
  assign sret = and_3_out ? demultiplexer_5_out_0 : 3'bz;  // Driver driver_11
  assign wfi = and_4_out ? demultiplexer_5_out_0 : 3'bz;  // Driver driver_12
  LED invalid (.in(demultiplexer_1_out_0));
  // Pins of 3 and 4 bits meet at lookuptable_1_out
  // Pins of 1 and 3 bits meet at ebreak
  // Pins of 1 and 3 bits meet at ecall
  // Pins of 1 and 3 bits meet at jalr
  // Pins of 1 and 3 bits meet at jal
  // Pins of 1 and 3 bits meet at mret
  // Pins of 1 and 3 bits meet at sfence_vma
  // Pins of 1 and 3 bits meet at sret
  // Pins of 1 and 3 bits meet at wfi
  // Pins of 1 and 3 bits meet at {op, 1'b1}
  // Pins of 1 and 3 bits meet at demultiplexer_5_out_0

  // Notes on the sheet:
  //   contents of lookuptable_1 (hex, n*v repeats v):
  //   0,0,0,5,15*0,2,79*0,1,0,0,0,4,7*0,6,0,0,0,3
  //   I
  //   B
  //   R
endmodule
