// Digital circuit 11.dig as structural Verilog
module _11 (
  input  clk,
  input  in_2,
  input  in_3,
  output out_4,
  output [7:0] out_5,
  output [7:0] out_6,
  output out_7,
  output [1:0] out_8,
  output out_9,
  output [7:0] out_10,
  output out_11,
  output [1:0] out_12,
  output [7:0] out_13
);

  wire i2c_master_1_scl, i2c_master_1_sda;

  i2c_master i2c_master_1 (
    .Dev_addr(7'b0000001), .mem_addr(8'h3), .RW(in_2), .on_off(in_3), .SDA_in(i2c_master_1_sda),
    .Data_in(8'hf), .Clock(clk), .SCL(i2c_master_1_scl), .SDA(i2c_master_1_sda), .Data_out(out_10),
    .status(out_11), .NACK(out_9), .stat(out_12));
  // i2c_slave i2c_slave_1: pin names not known; wires that end beside it: i2c_master_1_scl, i2c_master_1_sda, 7'b0000001, 8'h1, i2c_master_1_sda, out_4, out_5, out_6, out_7, out_8, out_13
  PullUp pullup_1 (.out(i2c_master_1_sda));

  // Notes on the sheet:
  //   clk: Hz: 2
endmodule
