// Digital circuit PLIC.dig as structural Verilog
module PLIC (
  input  Clock,
  input  TimerClock,
  input  [31:0] Addr_in,
  output [63:0] out_4
);

  wire [63:0] mtime_in;

  Add #(.Bits(64)) add_1 (.a(out_4), .b(64'h1), .c_i(TimerClock), .s(mtime_in));  // open: c_o
  Register #(.Bits(64)) mtime (.D(mtime_in), .C(TimerClock), .en(1'b1), .Q(out_4));
  RegisterFile #(.AddrBits(24), .Bits(32)) registerfile_1 ();  // open: Din, we, Rw, C, Ra, Rb, Da, Db

  // Other names for the same wires on the sheet: C = Clock; mtime_out[63:0] = out_4; TC = TimerClock
endmodule
