// Digital circuit boot-rom.dig as structural Verilog
module boot_rom (
  input  [7:0] Addr,
  input  En,
  output [31:0] Out_code
);

  wire [7:0] barrelshifter_1_out;

  BarrelShifter #(.Bits(8), .direction("right")) barrelshifter_1 (
    .in(Addr), .shift(4'b0010), .out(barrelshifter_1_out));
  ROM #(.AddrBits(8), .Bits(8)) rom_1 (.A(barrelshifter_1_out), .sel(En), .D(Out_code[7:0]));
  ROM #(.AddrBits(8), .Bits(8)) rom_2 (.A(barrelshifter_1_out), .sel(En), .D(Out_code[15:8]));
  ROM #(.AddrBits(8), .Bits(8)) rom_3 (.A(barrelshifter_1_out), .sel(En), .D(Out_code[23:16]));
  ROM #(.AddrBits(8), .Bits(8)) rom_4 (.A(barrelshifter_1_out), .sel(En), .D(Out_code[31:24]));

  // Notes on the sheet:
  //   contents of rom_1 (hex, n*v repeats v):
  //   7f,f3,13,b7,23,37,13,83,93,37,23,97,93,f3,37,13,f3,37,13,f3,6f
  //   ,3,13,33,13,93,33,33,23,37,13,83,b7,93,b3,37,23,73
  //   contents of rom_2 (hex, n*v repeats v):
  //   0,12,3,5,a0,e,e,2e,8e,e,20,7,87,93,2e,e,13,1e,e,13,0,a3,6,76,46
  //   ,2,73,63,a2,e,e,2e,27,87,8e,e,20
  //   contents of rom_3 (hex, n*v repeats v):
  //   0,0,f0,0,65,0,8e,e,e,0,de,0,87,57,0,8e,e,0,8e,4e,0,45,f0,c3,f6
  //   ,0,53,c3,65,0,8e,e,0,7,fe,0,de,20
  //   contents of rom_4 (hex, n*v repeats v):
  //   80,30,7,a0,0,b0,0,0,7d,b0,1,0,2,30,0,80,30,0,88,30,0,0,7,0,7,f8
  //   ,0,0,0,b0,0,0,0,71,0,b0,1,30
endmodule
