// Digital circuit i2c-slave.dig as structural Verilog
module i2c_slave (
  input  SCL,
  input  SDA,
  input  [6:0] Address,
  input  [7:0] Data_in,
  output SDA_out,
  output Out_en,
  output [7:0] Data_out,
  output [7:0] Addr_out,
  output invalidaddr,
  output [1:0] stat
);

  wire and_1_out, and_4_out, and_5_out, and_6_out, and_8_out, and_9_out, and_12_out, ask_in, comparator_1_eq,
       control_sig, data_bit, dstatus_en, i2c_master_readdata_2_status, i2c_master_senddata_1_status,
       or_2_out, rw, s1_end, s2_end, s2_read, s3_read, slave_s0, slave_s1, slave_s2, slave_s3, start_sig,
       status_change, stop_sig, xor_1_out;
  wire [1:0] dstatus, status_last, xor_2_out;
  wire [7:0] Addr_out_t, Data_out_t, i2c_master_readdata_1_data_out, i2c_master_readdata_2_data_out,
       i2c_master_readdata_3_data_out;

  and and_1 (and_1_out, control_sig, SDA);
  xor xor_1 (xor_1_out, SDA, data_bit);
  and and_2 (start_sig, control_sig, ~SDA);  // And
  and and_3 (control_sig, xor_1_out, SCL);
  D_FF d_ff_1 (.D(SDA), .C(SCL), .Q(data_bit));  // open: nQ
  or or_1 (stop_sig, and_1_out, invalidaddr);
  or or_2 (or_2_out, slave_s1, slave_s0);
  and and_4 (and_4_out, stop_sig, ~slave_s0);  // And
  and and_5 (and_5_out, start_sig, ~or_2_out, ~stop_sig);  // And
  _4_status_mechine _4_status_mechine_1 (
    .Clock(SCL), .nexten_0(start_sig), .nexten_1(s1_end), .nexten_2(s2_end), .nexten_3(Out_en),
    .direct_statusen(dstatus_en), .direct_status(dstatus), .falling_edge_status(4'b0111), .Status_cur(stat));
  i2c_master_readdata i2c_master_readdata_1 (
    .en(slave_s1), .Clock(SCL), .SDA_in(SDA), .SDA(SDA_out), .status(s1_end),
    .Data_out(i2c_master_readdata_1_data_out));
  Comparator #(.Bits(7)) comparator_1 (.a(Addr_out[7:1]), .b(Address), .eq(comparator_1_eq));  // open: gt, lt
  assign dstatus = and_4_out ? 2'b00 : 2'bz;  // Driver driver_1
  assign dstatus = and_5_out ? 2'b01 : 2'bz;  // Driver driver_2
  and and_6 (and_6_out, s1_end, slave_s1);
  and and_7 (invalidaddr, ~comparator_1_eq, slave_s1, s1_end);  // And
  assign Addr_out = and_6_out ? i2c_master_readdata_1_data_out : 8'bz;  // Driver driver_3
  D_FF d_ff_2 (.D(Addr_out[0]), .C(s1_end), .Q(rw));  // open: nQ
  assign dstatus_en = and_4_out ? 1'b1 : 1'bz;  // Driver driver_4
  assign dstatus_en = and_5_out ? 1'b1 : 1'bz;  // Driver driver_5
  Decoder #(.Selector_Bits(2)) decoder_1 (
    .sel(stat), .out_0(slave_s0), .out_1(slave_s1), .out_2(slave_s2), .out_3(slave_s3));
  and and_8 (and_8_out, s2_read, status_change);
  and and_9 (and_9_out, s3_read, status_change);
  Register #(.Bits(2)) register_1 (.D(stat), .C(~SCL), .en(1'b1), .Q(status_last));
  and and_10 (s2_read, slave_s2, ~rw);  // And
  i2c_master_readdata i2c_master_readdata_2 (
    .en(and_8_out), .Clock(SCL), .SDA_in(SDA), .SDA(SDA_out), .status(i2c_master_readdata_2_status),
    .Data_out(i2c_master_readdata_2_data_out));
  Register #(.Bits(8)) register_2 (.D(Addr_out), .C(s2_read), .en(s2_end), .Q(Addr_out_t));
  assign xor_2_out = stat ^ status_last;  // XOr xor_2, 2 bits wide
  and and_11 (s3_read, slave_s3, ~rw);  // And
  i2c_master_readdata i2c_master_readdata_3 (
    .en(and_9_out), .Clock(SCL), .SDA_in(SDA), .SDA(SDA_out), .status(Out_en),
    .Data_out(i2c_master_readdata_3_data_out));
  Register #(.Bits(8)) register_3 (.D(Addr_out), .C(s3_read), .en(Out_en), .Q(Data_out_t));
  Comparator #(.Bits(2)) comparator_2 (.a(xor_2_out), .b(2'b00), .gt(status_change));  // open: eq, lt
  assign s2_end = ~rw ? i2c_master_readdata_2_status : 1'bz;  // DriverInvSel driverinvsel_1
  assign Addr_out = s2_read ? i2c_master_readdata_2_data_out : 8'bz;  // Driver driver_6
  and and_12 (and_12_out, slave_s2, status_change, rw);
  assign Addr_out = s3_read ? i2c_master_readdata_3_data_out : 8'bz;  // Driver driver_7
  assign Data_out = ~rw ? Data_out_t : 8'bz;  // DriverInvSel driverinvsel_2
  i2c_master_senddata i2c_master_senddata_1 (
    .Data_in(Data_in), .en(and_12_out), .Clock(SCL), .SDA_in(SDA), .SDA(SDA_out),
    .status(i2c_master_senddata_1_status), .ack(ask_in));
  assign s2_end = rw ? i2c_master_senddata_1_status : 1'bz;  // Driver driver_8

  // Other names for the same wires on the sheet: Addr_invalid = invalidaddr; Addr_self[6:0] = Address;
  //   byte_out[7:0] = Addr_out; dev_addr[6:0] = Addr_out[7:1]; I2C_status[1:0] = stat; s3_end = Out_en; scl_in = SCL;
  //   sda_in = SDA

  // Notes on the sheet:
  //   s0: wait start
  //   s1: read dev address
  //   s2: read write mem address or send data
  //   s3: read write data
endmodule
