// Digital circuit instruction-decoder.dig as structural Verilog
module instruction_decoder (
  input  [31:0] Instruction_In,
  output [7:0] mechie_op,
  output [4:0] rd,
  output [4:0] rs1,
  output [4:0] rs2,
  output [6:0] imm_2531,
  output [19:0] imm_1231,
  output [11:0] imm_2032,
  output invalid,
  output [5:0] csr_op,
  output [8:0] jmp_op,
  output [18:0] alu_op,
  output [8:0] SL_op,
  output Cust_op
);

  wire _3bit_decoder_3__0, _3bit_decoder_3__5, _3bit_decoder_6__5, _3bit_decoder_7__0, and_1_out, and_2_out,
       comparator_1_eq, decoder_1_out_1, decoder_1_out_2, decoder_1_out_3, decoder_1_out_5, decoder_1_out_7,
       decoder_1_out_8, decoder_1_out_11, nor_1_out, not_1_out, not_2_out, not_3_out, not_4_out;
  wire [3:0] lookuptable_1_out;

  LookUpTable #(.Bits(4)) lookuptable_1 (
    .in0(Instruction_In[0]), .in1(Instruction_In[1]), .in2(Instruction_In[2]), .in3(Instruction_In[3]),
    .in4(Instruction_In[4]), .in5(Instruction_In[5]), .in6(Instruction_In[6]), .out(lookuptable_1_out));
  Decoder #(.Selector_Bits(4)) decoder_1 (
    .sel(lookuptable_1_out), .out_0(invalid), .out_1(decoder_1_out_1), .out_2(decoder_1_out_2),
    .out_3(decoder_1_out_3), .out_4(jmp_op[1]), .out_5(decoder_1_out_5), .out_6(jmp_op[0]),
    .out_7(decoder_1_out_7), .out_8(decoder_1_out_8), .out_9(jmp_op[8]), .out_10(SL_op[0]),
    .out_11(decoder_1_out_11), .out_15(Cust_op));  // open: out_12, out_13, out_14
  _3bit_decoder _3bit_decoder_1 (
    .EN(decoder_1_out_11), .Din(Instruction_In[14:12]), ._0(mechie_op[6]), ._1(mechie_op[7]), ._2(invalid),
    ._3(invalid), ._4(invalid), ._5(invalid), ._6(invalid), ._7(invalid));
  _3bit_decoder _3bit_decoder_2 (
    .EN(decoder_1_out_8), .Din(Instruction_In[14:12]), ._0(SL_op[6]), ._1(SL_op[7]), ._2(SL_op[8]),
    ._3(invalid), ._4(invalid), ._5(invalid), ._6(invalid), ._7(invalid));
  not not_1 (not_1_out, Instruction_In[30]);
  _3bit_decoder _3bit_decoder_3 (
    .EN(decoder_1_out_7), .Din(Instruction_In[14:12]), ._0(_3bit_decoder_3__0), ._1(alu_op[2]),
    ._2(alu_op[3]), ._3(alu_op[4]), ._4(alu_op[9]), ._5(_3bit_decoder_3__5), ._6(alu_op[10]), ._7(alu_op[11]));
  _3bit_decoder _3bit_decoder_4 (
    .EN(decoder_1_out_5), .Din(Instruction_In[14:12]), ._0(SL_op[1]), ._1(SL_op[2]), ._2(SL_op[3]),
    ._3(invalid), ._4(SL_op[4]), ._5(SL_op[5]), ._6(invalid), ._7(invalid));
  _3bit_decoder _3bit_decoder_5 (
    .EN(decoder_1_out_1), .Din(Instruction_In[14:12]), ._0(jmp_op[2]), ._1(jmp_op[3]), ._2(invalid),
    ._3(invalid), ._4(jmp_op[4]), ._5(jmp_op[5]), ._6(jmp_op[6]), ._7(jmp_op[7]));
  _3bit_decoder _3bit_decoder_6 (
    .EN(decoder_1_out_2), .Din(Instruction_In[14:12]), ._0(alu_op[5]), ._1(alu_op[14]), ._2(alu_op[15]),
    ._3(alu_op[16]), ._4(alu_op[6]), ._5(_3bit_decoder_6__5), ._6(alu_op[7]), ._7(alu_op[8]));
  _3bit_decoder _3bit_decoder_7 (
    .EN(decoder_1_out_3), .Din(Instruction_In[14:12]), ._0(_3bit_decoder_7__0), ._1(csr_op[0]),
    ._2(csr_op[1]), ._3(csr_op[2]), ._4(invalid), ._5(csr_op[3]), ._6(csr_op[4]), ._7(csr_op[5]));
  nor nor_1 (nor_1_out, Instruction_In[25], Instruction_In[26], Instruction_In[27], Instruction_In[28], Instruction_In[29], Instruction_In[30], Instruction_In[31], Instruction_In[21], Instruction_In[22], Instruction_In[23], Instruction_In[24]);
  Comparator #(.Bits(7)) comparator_1 (
    .a(Instruction_In[31:25]), .b(7'b0001001), .eq(comparator_1_eq));  // open: gt, lt
  Comparator #(.Bits(32)) comparator_2 (.a(Instruction_In), .b(32'h10200073), .eq(mechie_op[4]));  // open: gt, lt
  Comparator #(.Bits(32)) comparator_3 (.a(Instruction_In), .b(32'h30200073), .eq(mechie_op[2]));  // open: gt, lt
  Comparator #(.Bits(32)) comparator_4 (.a(Instruction_In), .b(32'h10500073), .eq(mechie_op[5]));  // open: gt, lt
  not not_2 (not_2_out, Instruction_In[20]);
  and and_1 (and_1_out, nor_1_out, Instruction_In[20]);
  and and_2 (and_2_out, nor_1_out, not_2_out);
  assign alu_op[0] = _3bit_decoder_3__0 ? not_1_out : 1'bz;  // Driver driver_1
  assign alu_op[1] = _3bit_decoder_3__0 ? Instruction_In[30] : 1'bz;  // Driver driver_2
  PullDown pulldown_1 (.out(_3bit_decoder_3__0));
  PullDown pulldown_2 (.out(_3bit_decoder_3__5));
  assign mechie_op[3] = _3bit_decoder_7__0 ? comparator_1_eq : 1'bz;  // Driver driver_3
  PullDown pulldown_3 (.out(_3bit_decoder_6__5));
  assign mechie_op[0] = _3bit_decoder_7__0 ? and_1_out : 1'bz;  // Driver driver_4
  assign mechie_op[1] = _3bit_decoder_7__0 ? and_2_out : 1'bz;  // Driver driver_5
  not not_3 (not_3_out, Instruction_In[30]);
  not not_4 (not_4_out, Instruction_In[30]);
  PullDown pulldown_4 (.out(_3bit_decoder_7__0));
  PullDown #(.Bits(9)) pulldown_5 (.out(SL_op));
  assign alu_op[17] = _3bit_decoder_6__5 ? not_4_out : 1'bz;  // Driver driver_6
  assign alu_op[18] = _3bit_decoder_6__5 ? Instruction_In[30] : 1'bz;  // Driver driver_7
  assign alu_op[12] = _3bit_decoder_3__5 ? Instruction_In[30] : 1'bz;  // Driver driver_8
  assign alu_op[13] = _3bit_decoder_3__5 ? not_3_out : 1'bz;  // Driver driver_9
  PullDown #(.Bits(19)) pulldown_6 (.out(alu_op));
  PullDown #(.Bits(9)) pulldown_7 (.out(jmp_op));
  PullDown #(.Bits(6)) pulldown_8 (.out(csr_op));
  PullDown #(.Bits(8)) pulldown_9 (.out(mechie_op));

  assign imm_1231 = Instruction_In[31:12];
  assign imm_2032 = Instruction_In[31:20];
  assign imm_2531 = Instruction_In[31:25];
  assign rd = Instruction_In[11:7];
  assign rs1 = Instruction_In[19:15];
  assign rs2 = Instruction_In[24:20];

  // Other names for the same wires on the sheet: add = alu_op[0]; addi = alu_op[5]; and = alu_op[11];
  //   andi = alu_op[8]; auipc = jmp_op[8]; beq = jmp_op[2]; bge = jmp_op[5]; bgeu = jmp_op[7]; blt = jmp_op[4];
  //   bltu = jmp_op[6]; bne = jmp_op[3]; csrrc = csr_op[2]; csrrci = csr_op[5]; csrrs = csr_op[1]; csrrsi = csr_op[4];
  //   csrrw = csr_op[0]; csrrwi = csr_op[3]; ebreak = mechie_op[0]; ecall = mechie_op[1]; fence = mechie_op[6];
  //   fence_i = mechie_op[7]; instructionCode[31:0] = Instruction_In; funct3[2:0] = Instruction_In[14:12];
  //   imm_12_31[19:0] = Instruction_In[31:12]; imm_20_31[11:0] = Instruction_In[31:20];
  //   imm_25_31[6:0] = Instruction_In[31:25]; _30 = Instruction_In[30]; invlid_op = invalid; jal = jmp_op[0];
  //   jalr = jmp_op[1]; lb = SL_op[1]; lbu = SL_op[4]; lh = SL_op[2]; lhu = SL_op[5]; lui = SL_op[0]; lw = SL_op[3];
  //   mret = mechie_op[2]; or = alu_op[10]; ori = alu_op[7]; sb = SL_op[6]; sfence_vma = mechie_op[3]; sh = SL_op[7];
  //   sll = alu_op[2]; slli = alu_op[14]; slt = alu_op[3]; slti = alu_op[15]; sltiu = alu_op[16]; sltu = alu_op[4];
  //   sra = alu_op[12]; srai = alu_op[18]; sret = mechie_op[4]; srl = alu_op[13]; srli = alu_op[17]; sub = alu_op[1];
  //   sw = SL_op[8]; wfi = mechie_op[5]; xor = alu_op[9]; xori = alu_op[6]

  // Notes on the sheet:
  //   contents of lookuptable_1 (hex, n*v repeats v):
  //   0,0,0,5,11*0,b,0,0,0,2,0,0,0,9,11*0,8,15*0,7,0,0,0,a,43*0,1,0,0,0
  //   ,4,7*0,6,0,0,0,3,11*0,f
  //   U
  //   R
  //   I
  //   B
  //   S
endmodule
