// Digital circuit int-except-unit.dig as structural Verilog
module int_except_unit (
  input  [31:0] Data_csr,
  input  WE_CSR,
  input  [11:0] Addr_csrw,
  input  Clock,
  input  [11:0] Addr_csr1,
  input  [11:0] Addr_csr2,
  input  [31:0] Exception_code,
  input  Interrupt_timer,
  input  Interrupt_soft,
  input  Interrupt_peripheral,
  input  [31:0] PC_Addr,
  input  [31:0] PC_ip,
  input  [31:0] PC_next,
  input  mret,
  input  [31:0] mip_in,
  input  mip_en,
  output [31:0] Out_csr1,
  output [31:0] Out_csr2,
  output En_jmp,
  output [31:0] Addr_jmp,
  output [31:0] mip_out
);

  wire and_1_out, and_6_out, and_7_out, and_8_out, Do_intperipheral, Do_intsoft, Do_inttimer, EN_excep,
       EN_ie, EN_int, enter_excep, int_peripheral, int_soft, int_timer, mcause_en, mepc_en, mie_en, mip_en_t,
       mstatus_en, mtval, mtvec_en, not_2_out, or_4_out, raen0, raen1, raen2, raen3, raen4, raen5, raen6,
       raen7, rben0, rben1, rben2, rben3, rben4, rben5, rben6, rben7, WE_common, wen0, wen1, wen2, wen3,
       wen4, wen5, wen6, wen7;
  wire [11:0] Addr_cw;
  wire [30:0] int_code;
  wire [31:0] and_2_out, and_4_out, Data_common, mcause_data, mcause_in, mcause_out, mepc_data, mepc_in,
       mepc_out, mie_in, mie_out, mip_in_t, mstatus_in, mstatus_out, mtval_in, mtval_out, mtvec_in,
       mtvec_out, offset_jmp, Out_cc1, Out_cc2, vec_offset;

  and and_1 (and_1_out, EN_int, EN_ie);
  not not_1 (EN_excep, Exception_code[0]);
  or or_1 (EN_int, int_soft, int_timer, int_peripheral);
  or or_2 (enter_excep, and_1_out, EN_excep);
  PullUp #(.Bits(32)) pullup_1 (.out(Exception_code));
  csr_addr_spliter csr_addr_spliter_1 (
    .Addr_csr(Addr_csr1), .Out_0(raen0), .Out_1(raen1), .Out_2(raen2), .Out_3(raen3), .Out_4(raen4),
    .Out_5(raen5), .Out_6(raen6), .Out_7(raen7));
  csr_addr_spliter csr_addr_spliter_2 (
    .Addr_csr(Addr_csrw), .Out_0(wen0), .Out_1(wen1), .Out_2(wen2), .Out_3(wen3), .Out_4(wen4), .Out_5(wen5),
    .Out_6(wen6), .Out_7(wen7));
  Register #(.Bits(32)) mstatus (
    .D(mstatus_in), .C(Clock), .en(mstatus_en), .Q({mstatus_out[31:4], EN_ie, mstatus_out[2:0]}));
  assign {and_2_out[31:12], int_peripheral, and_2_out[10:8], int_timer, and_2_out[6:4], int_soft, and_2_out[2:0]} = mie_out & mip_in_t;  // And and_2, 32 bits wide
  assign mstatus_in = enter_excep ? {mstatus_out[31:8], EN_ie, mstatus_out[6:4], 1'b0, mstatus_out[2:0]} : 32'bz;  // Driver driver_1
  assign mtval_in = enter_excep ? PC_ip : 32'bz;  // Driver driver_2
  assign mstatus_in = mret ? {mstatus_out[31:8], 1'b1, mstatus_out[6:4], mstatus_out[7], mstatus_out[2:0]} : 32'bz;  // Driver driver_3
  assign mip_in_t = mip_out | {{20{1'b0}}, Interrupt_peripheral, 3'b000, Interrupt_timer, 3'b000, Interrupt_soft, 3'b000};  // Or or_3, 32 bits wide
  assign Out_csr1 = raen0 ? Out_cc1 : 32'bz;  // Driver driver_4
  assign Out_csr1 = raen2 ? mie_out : 32'bz;  // Driver driver_5
  assign Out_csr1 = raen4 ? mepc_out : 32'bz;  // Driver driver_6
  assign Out_csr1 = raen6 ? mtval_out : 32'bz;  // Driver driver_7
  assign Data_common = wen0 ? Data_csr : 32'bz;  // Driver driver_8
  assign mstatus_in = wen1 ? Data_csr : 32'bz;  // Driver driver_9
  assign mtvec_in = wen3 ? Data_csr : 32'bz;  // Driver driver_10
  assign mcause_in = wen5 ? Data_csr : 32'bz;  // Driver driver_11
  assign mip_in_t = wen7 ? Data_csr : 32'bz;  // Driver driver_12
  Register #(.Bits(32)) mie (.D(mie_in), .C(Clock), .en(mie_en), .Q(mie_out));
  assign mstatus_en = enter_excep ? 1'b1 : 1'bz;  // Driver driver_13
  assign mtval = enter_excep ? 1'b1 : 1'bz;  // Driver driver_14
  assign mstatus_en = mret ? 1'b1 : 1'bz;  // Driver driver_15
  assign Out_csr1 = raen1 ? {mstatus_out[31:4], EN_ie, mstatus_out[2:0]} : 32'bz;  // Driver driver_16
  assign Out_csr1 = raen3 ? mtvec_out : 32'bz;  // Driver driver_17
  assign Out_csr1 = raen5 ? mcause_out : 32'bz;  // Driver driver_18
  assign Out_csr1 = raen7 ? mip_out : 32'bz;  // Driver driver_19
  Register #(.Bits(32)) mtvec (.D(mtvec_in), .C(Clock), .en(mtvec_en), .Q(mtvec_out));
  LookUpTable #(.Bits(31)) lookuptable_1 (
    .in0(Interrupt_soft), .in1(Interrupt_timer), .in2(Interrupt_peripheral), .out(int_code));
  assign mcause_in = enter_excep ? mcause_data : 32'bz;  // Driver driver_20
  assign WE_common = wen0 ? WE_CSR : 1'bz;  // Driver driver_21
  assign mstatus_en = wen1 ? WE_CSR : 1'bz;  // Driver driver_22
  assign mtvec_en = wen3 ? WE_CSR : 1'bz;  // Driver driver_23
  assign mcause_en = wen5 ? WE_CSR : 1'bz;  // Driver driver_24
  assign mip_en_t = wen7 ? WE_CSR : 1'bz;  // Driver driver_25
  and and_3 (Do_intperipheral, ~EN_excep, int_peripheral);  // And
  assign mepc_in = enter_excep ? mepc_data : 32'bz;  // Driver driver_26
  assign Addr_jmp = mret ? mepc_out : 32'bz;  // Driver driver_27
  Register #(.Bits(32)) mepc (.D(mepc_in), .C(Clock), .en(mepc_en), .Q(mepc_out));
  assign mcause_en = enter_excep ? 1'b1 : 1'bz;  // Driver driver_28
  assign Addr_cw = wen0 ? Addr_csrw : 12'bz;  // Driver driver_29
  assign mepc_en = enter_excep ? 1'b1 : 1'bz;  // Driver driver_30
  assign and_4_out = mip_in & mip_out;  // And and_4, 32 bits wide
  csr_addr_spliter csr_addr_spliter_3 (
    .Addr_csr(Addr_csr2), .Out_0(rben0), .Out_1(rben1), .Out_2(rben2), .Out_3(rben3), .Out_4(rben4),
    .Out_5(rben5), .Out_6(rben6), .Out_7(rben7));
  assign mie_in = wen2 ? Data_csr : 32'bz;  // Driver driver_31
  assign mepc_in = wen4 ? Data_csr : 32'bz;  // Driver driver_32
  assign mtval_in = wen6 ? Data_csr : 32'bz;  // Driver driver_33
  Register #(.Bits(32)) mcause (.D(mcause_in), .C(Clock), .en(mcause_en), .Q(mcause_out));
  assign mcause_data = EN_excep ? {1'b0, Exception_code[31:1]} : 32'bz;  // Driver driver_34
  or or_4 (or_4_out, EN_excep, ~mtvec_out[0]);  // Or
  and and_5 (Do_intsoft, ~EN_excep, ~Do_intperipheral);  // And
  assign Addr_jmp = or_4_out ? {mtvec_out[31:2], 2'b00} : 32'bz;  // Driver driver_35
  Add #(.Bits(32)) add_1 (.a({mtvec_out[31:2], 2'b00}), .b(offset_jmp), .c_i(1'b0), .s(vec_offset));  // open: c_o
  assign mip_in_t = mip_en ? and_4_out : 32'bz;  // Driver driver_36
  assign mie_en = wen2 ? WE_CSR : 1'bz;  // Driver driver_37
  assign mepc_en = wen4 ? WE_CSR : 1'bz;  // Driver driver_38
  assign mtval = wen6 ? WE_CSR : 1'bz;  // Driver driver_39
  Register #(.Bits(32)) u_mtval (.D(mtval_in), .C(Clock), .en(mtval), .Q(mtval_out));
  assign mepc_data = EN_excep ? PC_Addr : 32'bz;  // Driver driver_40
  assign Out_csr2 = rben6 ? mtval_out : 32'bz;  // Driver driver_41
  not not_2 (not_2_out, EN_excep);
  and and_6 (and_6_out, Do_intperipheral, mtvec_out[0]);
  and and_7 (and_7_out, Do_intsoft, mtvec_out[0]);
  and and_8 (and_8_out, Do_inttimer, mtvec_out[0]);
  assign mip_en_t = mip_en ? WE_CSR : 1'bz;  // Driver driver_42
  assign Out_csr2 = rben0 ? Out_cc1 : 32'bz;  // Driver driver_43
  assign Out_csr2 = rben2 ? mie_out : 32'bz;  // Driver driver_44
  assign Out_csr2 = rben4 ? mepc_out : 32'bz;  // Driver driver_45
  Register #(.Bits(32)) mip (.D(mip_in_t), .C(Clock), .en(mip_en_t), .Q(mip_out));
  assign Addr_jmp = and_6_out ? vec_offset : 32'bz;  // Driver driver_46
  assign Addr_jmp = and_7_out ? vec_offset : 32'bz;  // Driver driver_47
  assign Addr_jmp = and_8_out ? vec_offset : 32'bz;  // Driver driver_48
  assign mcause_data = not_2_out ? {1'b1, int_code} : 32'bz;  // Driver driver_49
  and and_9 (Do_inttimer, ~EN_excep, ~Do_intsoft, ~Do_intperipheral);  // And
  assign Out_csr2 = rben1 ? {mstatus_out[31:4], EN_ie, mstatus_out[2:0]} : 32'bz;  // Driver driver_50
  assign Out_csr2 = rben3 ? mtvec_out : 32'bz;  // Driver driver_51
  assign Out_csr2 = rben5 ? mcause_out : 32'bz;  // Driver driver_52
  assign Out_csr2 = rben7 ? mip_out : 32'bz;  // Driver driver_53
  assign offset_jmp = and_6_out ? 32'h2c : 32'bz;  // Driver driver_54
  assign offset_jmp = and_7_out ? 32'hc : 32'bz;  // Driver driver_55
  assign offset_jmp = and_8_out ? 32'h1c : 32'bz;  // Driver driver_56
  RegisterFile #(.AddrBits(12), .Bits(32)) CSR_Registers (
    .Din(Data_common), .we(WE_common), .Rw(Addr_cw), .C(Clock), .Ra(Addr_csr1), .Rb(Addr_csr2), .Da(Out_cc1),
    .Db(Out_cc2));
  assign mepc_data = not_2_out ? PC_next : 32'bz;  // Driver driver_57
  or or_5 (En_jmp, EN_excep, mret);
  PullDown #(.Bits(32)) pulldown_1 (.out(Addr_jmp));

  // Other names for the same wires on the sheet: c = Clock; excep_code[30:0] = Exception_code[31:1];
  //   newmip (some bits) = {Interrupt_peripheral, Interrupt_timer, Interrupt_soft}; mip_set[31:0] = mip_in;
  //   mip_seten = mip_en; mstatus_out[3] = EN_ie; vec_mode = mtvec_out[0]; vec_base[31:2] = mtvec_out[31:2]

  // Notes on the sheet:
  //   contents of lookuptable_1 (hex, n*v repeats v):
  //   0,3,7,0,b
endmodule
