// Digital circuit memory-operation-unit.dig as structural Verilog
module memory_operation_unit (
  input  [8:0] MemOp_in,
  input  [31:0] Data_in,
  input  [31:0] rs1,
  input  [31:0] rs2,
  input  [11:0] Offset_12,
  input  [6:0] Offset_7,
  input  [4:0] Offset_5,
  input  [19:0] imm_20,
  output we_out,
  output [31:0] Addr_out,
  output [31:0] Mem_out,
  output [3:0] StoreByteSize_out,
  output oe_out,
  output RegWE_out,
  output [31:0] rd_out
);

  wire not_1_out, or_2_out;
  wire [31:0] and_1_out, and_3_out, barrelshifter_1_out, bitextender_1_out, bitextender_2_out,
       bitextender_3_out, bitextender_4_out, bitextender_5_out, bitextender_6_out, bitextender_7_out,
       driver_1_out, driver_2_out, driver_3_out, driver_4_out, offset, or_1_out;

  assign driver_1_out = StoreByteSize_out[0] ? 32'hff : 32'bz;  // Driver driver_1
  assign driver_2_out = StoreByteSize_out[1] ? 32'hffff : 32'bz;  // Driver driver_2
  assign driver_3_out = StoreByteSize_out[2] ? 32'hffffff : 32'bz;  // Driver driver_3
  assign driver_4_out = StoreByteSize_out[3] ? {32{1'b1}} : 32'bz;  // Driver driver_4
  assign or_1_out = driver_1_out | driver_2_out | driver_3_out | driver_4_out;  // Or or_1, 32 bits wide
  PullDown pulldown_1 (.out(we_out));
  assign and_1_out = or_1_out & Data_in;  // And and_1, 32 bits wide
  assign we_out = MemOp_in[1] ? 1'b0 : 1'bz;  // Driver driver_5
  assign we_out = MemOp_in[4] ? 1'b0 : 1'bz;  // Driver driver_6
  assign we_out = MemOp_in[2] ? 1'b0 : 1'bz;  // Driver driver_7
  assign we_out = MemOp_in[5] ? 1'b0 : 1'bz;  // Driver driver_8
  assign we_out = MemOp_in[3] ? 1'b0 : 1'bz;  // Driver driver_9
  assign rd_out = oe_out ? and_1_out : 32'bz;  // Driver driver_10
  or or_2 (or_2_out, MemOp_in[0], MemOp_in[1], MemOp_in[2], MemOp_in[3], MemOp_in[4], MemOp_in[5]);
  PullDown pulldown_2 (.out(we_out));
  BitExtender #(.inputBits(12), .outputBits(32)) bitextender_1 (.in(Offset_12), .out(bitextender_1_out));
  BitExtender #(.inputBits(12), .outputBits(32)) bitextender_2 (.in(Offset_12), .out(bitextender_2_out));
  BitExtender #(.inputBits(12), .outputBits(32)) bitextender_3 (.in(Offset_12), .out(bitextender_3_out));
  not not_1 (not_1_out, we_out);
  assign offset = MemOp_in[1] ? bitextender_1_out : 32'bz;  // Driver driver_11
  assign offset = MemOp_in[4] ? {{20{1'b0}}, Offset_12} : 32'bz;  // Driver driver_12
  assign offset = MemOp_in[2] ? bitextender_2_out : 32'bz;  // Driver driver_13
  assign offset = MemOp_in[5] ? {{20{1'b0}}, Offset_12} : 32'bz;  // Driver driver_14
  assign offset = MemOp_in[3] ? bitextender_3_out : 32'bz;  // Driver driver_15
  and and_2 (oe_out, or_2_out, not_1_out);
  assign StoreByteSize_out = MemOp_in[1] ? 4'b0001 : 4'bz;  // Driver driver_16
  assign StoreByteSize_out = MemOp_in[4] ? 4'b0001 : 4'bz;  // Driver driver_17
  assign StoreByteSize_out = MemOp_in[2] ? 4'b0011 : 4'bz;  // Driver driver_18
  assign StoreByteSize_out = MemOp_in[5] ? 4'b0011 : 4'bz;  // Driver driver_19
  assign StoreByteSize_out = MemOp_in[3] ? 4'b1111 : 4'bz;  // Driver driver_20
  assign we_out = MemOp_in[0] ? 1'b0 : 1'bz;  // Driver driver_21
  BitExtender #(.inputBits(20), .outputBits(32)) bitextender_4 (.in(imm_20), .out(bitextender_4_out));
  assign we_out = MemOp_in[6] ? 1'b1 : 1'bz;  // Driver driver_22
  assign we_out = MemOp_in[7] ? 1'b1 : 1'bz;  // Driver driver_23
  assign we_out = MemOp_in[8] ? 1'b1 : 1'bz;  // Driver driver_24
  BarrelShifter #(.Bits(32)) barrelshifter_1 (.in(bitextender_4_out), .shift(6'b001100), .out(barrelshifter_1_out));
  Add #(.Bits(32)) add_1 (.a(rs1), .b(offset), .c_i(1'b0), .s(Addr_out));  // open: c_o
  BitExtender #(.inputBits(12), .outputBits(32)) bitextender_5 (.in({Offset_7, Offset_5}), .out(bitextender_5_out));
  BitExtender #(.inputBits(12), .outputBits(32)) bitextender_6 (.in({Offset_7, Offset_5}), .out(bitextender_6_out));
  BitExtender #(.inputBits(12), .outputBits(32)) bitextender_7 (.in({Offset_7, Offset_5}), .out(bitextender_7_out));
  assign and_3_out = barrelshifter_1_out & 32'hfffff00;  // And and_3, 32 bits wide
  assign offset = MemOp_in[6] ? bitextender_5_out : 32'bz;  // Driver driver_25
  assign offset = MemOp_in[7] ? bitextender_6_out : 32'bz;  // Driver driver_26
  assign offset = MemOp_in[8] ? bitextender_7_out : 32'bz;  // Driver driver_27
  assign offset = MemOp_in[0] ? and_3_out : 32'bz;  // Driver driver_28
  assign StoreByteSize_out = MemOp_in[6] ? 4'b0001 : 4'bz;  // Driver driver_29
  assign StoreByteSize_out = MemOp_in[7] ? 4'b0011 : 4'bz;  // Driver driver_30
  assign StoreByteSize_out = MemOp_in[8] ? 4'b1111 : 4'bz;  // Driver driver_31
  assign StoreByteSize_out = MemOp_in[0] ? 4'b0000 : 4'bz;  // Driver driver_32

  assign Mem_out = rs2;
  assign RegWE_out = oe_out;

  // Other names for the same wires on the sheet: Addr[31:0] = Addr_out; bytesize[3:0] = StoreByteSize_out;
  //   dataout[31:0] = rd_out; lui = MemOp_in[0]; lb = MemOp_in[1]; lh = MemOp_in[2]; lw = MemOp_in[3];
  //   lbu = MemOp_in[4]; lhu = MemOp_in[5]; sb = MemOp_in[6]; sh = MemOp_in[7]; sw = MemOp_in[8]; oe = oe_out;
  //   we = we_out
endmodule
