// Digital circuit risc-v-computer.dig as structural Verilog
module risc_v_computer (
  input  clk,
  input  clk_2,
  input  in_11,
  input  [4:0] in_12,
  input  [31:0] in_16,
  input  in_17,
  input  in_19,
  input  in_22,
  input  in_23,
  input  in_24,
  input  in_25,
  output [31:0] out_1,
  output [31:0] out_2,
  output [31:0] out_3,
  output [4:0] out_4,
  output [4:0] out_5,
  output [31:0] out_6,
  output [31:0] out_7,
  output [31:0] out_8,
  output [31:0] debugreg_out,
  output [31:0] out_14,
  output [31:0] out_15,
  output [31:0] out_18,
  output [8:0] out_20,
  output [31:0] out_21,
  output [63:0] out_26,
  output [63:0] out_27
);

  wire addrflag_mem, and_1_out, and_4_out, ard_en, button_1_out, c, crd_en, Cust_op, gpio_out1, gpio_out2,
       gpio_out3, gpio_out4, gpio_out5, gpio_out6, gpio_out7, gpio_out8, gpio_out9, gpio_out10,
       int_peripheral, int_timer, jrd_en, lrd_en, memgpio_en, memplic_en, mip_seten, mret, nor_1_out,
       not_1_out, Oe_mem, Oe_memop, Oe_ssd, PC_EN, PC_except, PC_inited, PC_jmp, PC_jmpen, rd_en, We_mem;
  wire [3:0] storebytes_size;
  wire [4:0] driver_11_out, rd;
  wire [5:0] csr_op;
  wire [6:0] imm_7;
  wire [7:0] data_memssd, mechine_op;
  wire [8:0] jmp_op;
  wire [11:0] Addr_csr1, imm_12;
  wire [18:0] alu_op;
  wire [19:0] imm_20;
  wire [31:0] Addr_except, Addr_jmp, Addr_jmpto, ard_out, crd_out, Data_csr, data_memgpio, data_memplic,
       data_memrdin, Instrction_Reg_q, int_peripheralcode, jrd_out, lrd_out, mip_cur, mip_set, Out_csr1,
       Out_csr2, program_counter_1_pc_next;

  or or_1 (rd_en, jrd_en, ard_en, crd_en, lrd_en);
  or or_2 (PC_jmpen, PC_jmp, PC_except);
  assign Addr_jmpto = PC_except ? Addr_except : 32'bz;  // Driver driver_1
  not not_1 (not_1_out, PC_inited);
  assign out_2 = not_1_out ? 32'h80000000 : 32'bz;  // Driver driver_2
  assign out_6 = jrd_en ? jrd_out : 32'bz;  // Driver driver_3
  assign out_6 = ard_en ? ard_out : 32'bz;  // Driver driver_4
  assign out_6 = crd_en ? crd_out : 32'bz;  // Driver driver_5
  assign out_6 = lrd_en ? lrd_out : 32'bz;  // Driver driver_6
  program_counter program_counter_1 (
    .En(PC_EN), .Clock(c), .Addr_set(out_2), .Addr_jmp(Addr_jmpto), .En_jmp(PC_jmpen),
    .PC_next(program_counter_1_pc_next));
  and and_1 (and_1_out, PC_jmp, ~PC_except);  // And
  instruction_decoder instruction_decoder_1 (
    .Instruction_In(out_3), .EN(PC_EN), .mechie_op(mechine_op), .rd(rd), .rs1(out_4), .rs2(out_5),
    .imm_2531(imm_7), .imm_1231(imm_20), .imm_2032(imm_12), .invalid(out_14), .csr_op(csr_op),
    .jmp_op(jmp_op), .alu_op(alu_op), .SL_op(out_20), .Cust_op(Cust_op));
  assign out_1 = not_1_out ? 32'h80000004 : 32'bz;  // Driver driver_7
  assign Addr_jmpto = and_1_out ? Addr_jmp : 32'bz;  // Driver driver_8
  assign out_1 = PC_inited ? program_counter_1_pc_next : 32'bz;  // Driver driver_9
  mechine_op_unit mechine_op_unit_1 (.mechine_op(mechine_op), .mret(mret));
  Register #(.Bits(32)) Instrction_Reg (.D(out_1), .C(c), .en(PC_EN), .Q(Instrction_Reg_q));
  LED led_1 (.in(gpio_out1));
  LED led_2 (.in(gpio_out2));
  LED led_3 (.in(gpio_out3));
  LED led_4 (.in(gpio_out4));
  LED led_5 (.in(gpio_out5));
  LED led_6 (.in(gpio_out6));
  LED led_7 (.in(gpio_out7));
  addr_compare addr_compare_1 (.Addr_in1(out_1), .Addr_in2(32'h2000078));  // open: Eq_out
  assign out_2 = PC_inited ? Instrction_Reg_q : 32'bz;  // Driver driver_10
  instuction_jump_unit instuction_jump_unit_1 (
    .jmp_op(jmp_op), .PC_cur(out_2), .PC_next(out_1), .rs1_in(out_7), .rs2_in(out_8), .Imm12_in(imm_12),
    .Imm20_in(imm_20), .Imm7_in(imm_7), .offset_5(rd), .Addr_jmp(Addr_jmp), .rd_out(jrd_out),
    .EN_out(jrd_en), .En_jmp(PC_jmp));
  cust_ctrl cust_ctrl_1 (.op_code(out_3), .cust_code(Cust_op), .Clock(c), .PC_init(PC_inited));
  csr csr_1 (
    .CSRCode_in(csr_op), .Data_in(out_7), .Csr_Addr(imm_12), .Imm5_in(out_4), .Clock(c),
    .Data_temp(Out_csr1), .En(crd_en), .Addr_csr(Addr_csr1), .Out_rd(crd_out), .Out_csr(Data_csr));
  assign c = ~in_22 ? clk_2 : 1'bz;  // DriverInvSel driverinvsel_1
  assign driver_11_out = rd_en ? rd : 5'bz;  // Driver driver_11
  risc_v_registers risc_v_registers_1 (
    .OE_P1(out_4), .Din(out_6), .Clock(c), .WE(driver_11_out), .OE_P2(out_5), .OE_P3(in_12),
    .Output_P1(out_7), .Output_P2(out_8), .Output_P3(debugreg_out));
  memory memory_1 (
    .Addr(out_18), .Data_in(out_21), .WE(We_mem), .OE(Oe_mem), .ByteSize_in(storebytes_size), .Clock(c),
    .Addr_PC(out_2), .OE_PC(addrflag_mem), .Data_out(out_15), .DataPC_out(out_3));
  assign c = in_22 ? button_1_out : 1'bz;  // Driver driver_12
  Button button_1 (.out(button_1_out));
  // boot_rom boot_rom_1: pin names not known; wires that end beside it: out_2[23:0], out_2[31], out_3
  assign PC_EN = ~in_22 ? 1'b1 : 1'bz;  // DriverInvSel driverinvsel_2
  int_except_unit int_except_unit_1 (
    .Data_csr(Data_csr), .WE_CSR(crd_en), .Addr_csrw(Addr_csr1), .Clock(c), .Addr_csr1(Addr_csr1),
    .Addr_csr2({12{1'b0}}), .Exception_code(out_14), .PC_Addr(out_2), .PC_ip(out_3), .PC_next(out_1),
    .mret(mret), .mip_in(mip_set), .mip_en(mip_seten), .Out_csr1(Out_csr1), .Out_csr2(Out_csr2),
    .En_jmp(PC_except), .Addr_jmp(Addr_except), .mip_out(mip_cur));  // open: mie_out, ecode_out, timer_en, mepc_out
  assign PC_EN = in_22 ? in_11 : 1'bz;  // Driver driver_13
  ROM #(.AddrBits(24), .Bits(8)) Program_Rom (.A(out_18[23:0]), .sel(Oe_ssd), .D(data_memssd));
  and and_2 (addrflag_mem, out_2[25], ~out_2[31]);  // And
  alu alu_1 (
    .Alu_in(alu_op), .rs1_in(out_7), .rs2_in(out_8), .Imm12_in(imm_12), .Clock(c), .rd_out(ard_out),
    .EN_out(ard_en), .InvlidOP_out(out_14));
  memory_operation_unit memory_operation_unit_1 (
    .MemOp_in(out_20), .Data_in(data_memrdin), .rs1(out_7), .rs2(out_8), .Offset_12(imm_12),
    .Offset_7(imm_7), .Offset_5(rd), .imm_20(imm_20), .we_out(We_mem), .Addr_out(out_18), .Mem_out(out_21),
    .StoreByteSize_out(storebytes_size), .oe_out(Oe_memop), .RegWE_out(lrd_en), .rd_out(lrd_out));
  PLIC plic_1 (
    .Clock(c), .TimerClock(clk), .Addr_w(out_18), .Data_in(out_21), .WE(We_mem), .Addr_r1(out_18),
    .mip_in(mip_cur), .perint_code(int_peripheralcode), .Out_ra(data_memplic), .Out_en(memplic_en),
    .mip_set(mip_set), .mip_seten(mip_seten), .int_timer(int_timer), .gate_peripheral(int_peripheral),
    .mtimcmp(out_26), .mtime(out_27));
  assign out_18 = in_17 ? in_16 : 32'bz;  // Driver driver_14
  nor nor_1 (nor_1_out, out_18[31], out_18[30]);
  and and_3 (Oe_ssd, out_18[30], Oe_memop);
  and and_4 (and_4_out, nor_1_out, Oe_memop);
  or or_3 (Oe_mem, and_4_out, in_19);
  assign data_memrdin = memplic_en ? data_memplic : 32'bz;  // Driver driver_15
  assign data_memrdin = Oe_mem ? out_15 : 32'bz;  // Driver driver_16
  gpio gpio_1 (
    .Clock(c), .Addr_w(out_18), .Data_in(out_21), .we(We_mem), .Addr_rd(out_18), .int_gate(int_peripheral),
    .GPIO1_in(1'b0), .GPIO2_in(1'b0), .GPIO3_in(1'b0), .GPIO4_in(1'b0), .GPIO5_in(1'b0), .GPIO6_in(1'b0),
    .GPIO7_in(1'b0), .GPIO8_in(in_23), .GPIO9_in(in_24), .GPIO10_in(in_25), .Out_rd(data_memgpio),
    .Out_en(memgpio_en), .perint_code(int_peripheralcode), .GPIO1_out(gpio_out1), .GPIO2_out(gpio_out2),
    .GPIO3_out(gpio_out3), .GPIO4_out(gpio_out4), .GPIO5_out(gpio_out5), .GPIO6_out(gpio_out6),
    .GPIO7_out(gpio_out7), .GPIO8_out(gpio_out8), .GPIO9_out(gpio_out9), .GPIO10_out(gpio_out10));
  assign data_memrdin = Oe_ssd ? {{24{1'b0}}, data_memssd} : 32'bz;  // Driver driver_17
  assign data_memrdin = memgpio_en ? data_memgpio : 32'bz;  // Driver driver_18

  // Other names for the same wires on the sheet: Addr_csrw[11:0] = Addr_csr1; data_mem[31:0] = out_21;
  //   data_memrd[31:0] = out_15; debug = in_22; gpio_in8 = in_23; gpio_in9 = in_24; gpio_in10 = in_25;
  //   instruction_code[31:0] = out_3; Invalid_op[31:0] = out_14; addr_iop[23:0] = out_18[23:0];
  //   mem_addr[31:0] = out_18; addrflag_ssd = out_18[30]; addrflag_peripheral = out_18[31]; mem_op[8:0] = out_20;
  //   Oe_debug = in_19; addr_real[23:0] = out_2[23:0]; PC_exec[31:0] = out_2; addrflag_memtmp = out_2[25];
  //   addrflag_boot = out_2[31]; PC_next[31:0] = out_1; rd_out[31:0] = out_6; reg_debug[4:0] = in_12;
  //   rs1[4:0] = out_4; rs1_data[31:0] = out_7; rs2[4:0] = out_5; rs2_data[31:0] = out_8; Timer_clock = clk

  // Notes on the sheet:
  //   clk: Hz: 100
  //   clk_2: Hz: 50000
  //   Reg-Write-Bus
  //   Instruction Program Counter Bus
  //   contents of Program_Rom (hex, n*v repeats v):
  //   97,7,0,0,93,87,c7,2,93,87,17,0,f3,93,57,30,37,2e,0,0,13,e,8e,80
  //   ,f3,13,e,30,37,1,0,1,ef,0,40,56,f3,13,45,30,67,80,0,0,ef,0,80
  //   ,33,73,0,20,30,13,0,0,0,13,0,0,0,13,0,0,0,13,0,0,0,13,0,0,0,ef
  //   ,0,0,32,73,0,20,30,13,0,0,0,13,0,0,0,ef,0,40,32,73,0,20,30,13
  //   ,1,1,ff,13,5,f0,7,23,26,11,0,ef,0,c0,20,b7,17,0,2,83,a7,7,85,63
  //   ,8c,7,6,23,24,81,0,37,14,0,2,83,27,84,84,63,9c,7,2,ef,0,40,24
  //   ,13,65,f5,7,ef,0,0,23,93,7,10,0,23,24,f4,84,37,6,0,2,3,24,81,0
  //   ,83,20,c1,0,13,6,6,6,13,5,40,1f,93,5,0,0,13,1,1,1,6f,0,c0,3b,ef
  //   ,0,0,21,13,75,5,f8,ef,0,c0,1f,37,6,0,2,23,24,4,84,3,24,81,0,83
  //   ,20,c1,0,13,6,6,6,13,5,40,1f,93,5,0,0,13,1,1,1,6f,0,c0,38,ef,0,0
  //   ,1e,13,75,5,f8,ef,0,c0,1c,b7,17,0,2,3,a5,c7,84,13,5,15,0,13,7
  //   ,70,0,63,48,a7,2,13,7,5,0,93,5,10,0,23,a6,e7,84,ef,0,80,16,37
  //   ,6,0,2,83,20,c1,0,13,6,6,6,13,5,40,1f,93,5,0,0,13,1,1,1,6f,0,0
  //   ,34,13,7,10,0,13,5,7,0,6f,f0,1f,fd,13,1,1,ff,13,5,a0,0,23,26,11
  //   ,0,ef,0,80,18,b7,17,0,2,23,a8,a7,84,83,20,c1,0,13,1,1,1,6f,0,0
  //   ,19,13,1,1,ff,13,5,f0,7,23,22,91,0,23,20,21,1,23,26,11,0,23,24
  //   ,81,0,b7,14,0,2,ef,0,0,f,13,9,80,0,13,5,a0,0,ef,0,80,14,23,a8
  //   ,a4,84,13,4,10,0,63,a,5,4,ef,0,c0,12,13,65,f5,7,ef,0,80,11,93
  //   ,5,0,0,13,5,40,1f,ef,0,c0,37,ef,0,40,11,13,75,5,f8,ef,0,0,10,13
  //   ,5,40,1f,93,5,0,0,ef,0,40,36,13,5,a0,0,ef,0,40,10,23,a8,a4,84
  //   ,13,4,10,0,e3,10,5,fc,6f,0,c0,0,83,a7,4,85,e3,90,7,fa,13,5,4,0
  //   ,93,5,10,0,ef,0,80,8,13,5,40,1f,93,5,0,0,ef,0,c0,32,13,5,4,0,93
  //   ,5,0,0,13,4,14,0,ef,0,c0,6,e3,18,24,fd,6f,f0,1f,f7,13,1,1,ff,23
  //   ,26,11,0,ef,0,80,2b,37,6,0,2,93,5,0,0,13,6,6,6,13,5,40,1f,ef,0
  //   ,80,23,b7,5,0,2,93,85,85,14,13,5,10,0,ef,0,40,b,6f,0,0,0,63,8e
  //   ,5,0,b7,7,0,a0,13,5,f5,ff,3,a7,7,0,b3,95,a5,0,b3,e5,e5,0,23,a0
  //   ,b7,0,67,80,0,0,b7,7,0,a0,23,a0,a7,0,67,80,0,0,37,7,0,a0,13,5
  //   ,f5,ff,93,7,10,0,13,7,47,0,b3,97,a7,0,3,27,7,0,63,8a,5,0,33,67
  //   ,f7,0,b7,7,0,a0,23,a2,e7,0,67,80,0,0,93,c7,f7,ff,33,f7,e7,0,b7
  //   ,7,0,a0,23,a2,e7,0,67,80,0,0,b7,7,0,a0,23,a2,a7,0,67,80,0,0,b7
  //   ,7,0,a0,3,a5,47,0,67,80,0,0,37,7,0,a0,13,5,f5,ff,93,7,10,0,b3
  //   ,97,a7,0,3,25,47,0,33,f5,a7,0,67,80,0,0,b7,7,0,a0,23,a4,7,0,67
  //   ,80,0,0,b7,7,0,2,13,15,25,0,93,87,47,7e,b3,87,a7,0,37,17,0,2,23
  //   ,a0,b7,0,3,25,47,85,93,7,f0,7f,63,f4,a7,0,67,80,0,0,b7,17,0,0
  //   ,93,87,7,80,33,65,f5,0,23,2a,a7,84,6f,f0,9f,ce,37,17,0,2,83,27
  //   ,47,85,93,e7,7,8,13,6,5,0,b7,16,0,2,13,85,7,0,23,ac,c6,84,23,2a
  //   ,f7,84,6f,f0,5f,cc,67,80,0,0,b7,17,0,2,83,a7,87,85,63,84,7,0,67
  //   ,80,7,0,67,80,0,0,b7,17,0,b0,3,a7,7,0,b7,7,0,2,13,17,27,0,93,87
  //   ,47,7e,b3,87,e7,0,83,a7,7,0,63,84,7,0,67,80,7,0,67,80,0,0,13,1,1
  //   ,ff,23,22,91,0,23,20,21,1,b7,4,0,2,37,9,0,b0,93,84,84,7f,13,9
  //   ,89,0,23,24,81,0,23,26,11,0,13,84,84,0,3,27,9,0,93,84,84,5,83
  //   ,26,49,0,83,27,4,0,63,8c,7,0,3,26,c4,ff,63,e8,c6,0,63,12,d6,4
  //   ,3,26,84,ff,63,7e,c7,2,13,4,4,1,e3,10,94,fe,13,6,47,6,33,37,e6
  //   ,0,b7,7,0,b0,33,7,d7,0,83,20,c1,0,3,24,81,0,23,a2,e7,0,23,a0,c7
  //   ,0,83,24,41,0,3,29,1,0,13,1,1,1,67,80,0,0,e7,80,7,0,13,4,4,1,23
  //   ,28,4,fe,3,27,9,0,83,26,49,0,e3,1c,94,f8,6f,f0,9f,fb,b7,7,0,b0
  //   ,3,a5,87,0,83,a5,c7,0,67,80,0,0,b7,7,0,b0,3,a5,7,0,83,a5,47,0
  //   ,67,80,0,0,b7,7,0,b0,23,a2,b7,0,23,a0,a7,0,67,80,0,0,37,8,0,2
  //   ,13,8,88,7f,13,7,88,0,93,7,0,0,93,8,50,0,83,26,7,0,63,8c,6,0,93
  //   ,87,17,0,13,7,7,1,e3,98,17,ff,13,5,10,0,67,80,0,0,b7,6,0,b0,3
  //   ,a7,86,0,93,86,86,0,83,a6,46,0,33,5,a7,0,93,97,47,0,33,37,e5,0
  //   ,b3,86,b6,0,33,8,f8,0,33,7,d7,0,23,20,a8,0,23,24,c8,0,23,22,e8
  //   ,0,13,5,0,0,67,80,0,0,37,7,0,b0,83,27,87,0,13,86,c7,12,13,7,87
  //   ,0,3,27,47,0,b3,37,f6,0,b7,6,0,b0,33,87,e7,0,37,5,0,2,b7,7,0,2
  //   ,23,a2,e6,0,23,a0,c6,0,93,87,87,7f,13,5,45,3a,23,a4,7,0,23,ac
  //   ,7,0,23,a4,7,2,23,ac,7,2,23,a4,7,4,6f,f0,1f,e1,b7,7,0,b0,83,a6
  //   ,87,0,3,a7,c7,0,33,6,d5,0,b3,85,e5,0,33,35,a6,0,b3,7,b5,0,63,74
  //   ,f7,2,b7,6,0,b0,93,86,86,0,13,0,0,0,3,a7,46,0,e3,6c,f7,fe,63,16
  //   ,f7,0,3,a7,6,0,e3,66,c7,fe,67,80,0,0,e3,9e,e7,fe,e3,ec,c6,fc,67
  //   ,80,0,0,13,1,1,ff,23,26,11,0,ef,f0,9f,c9,10,7*0,3,7a,52,0,1,7c
  //   ,1,1,1b,d,2,0,38,0,0,0,18,0,0,0,b4,fa,ff,ff,e8,4*0,44,e,10,48
  //   ,81,1,54,88,2,68,a,c8,44,c1,50,e,0,44,b,58,c8,44,c1,50,e,0,44
  //   ,e,10,81,1,2,38,a,c1,50,e,0,44,b,0,0,0,18,0,0,0,54,0,0,0,60,fb
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  //   Memory Bus
endmodule
