// Digital circuit tt.dig as structural Verilog
module tt (
  input  C,
  input  timeclk,
  input  [7:0] in_3,
  input  [31:0] in_4,
  output [31:0] out_5,
  output out_6,
  output out_7,
  output [2:0] out_8,
  output [7:0] out_9,
  output [31:0] out_10,
  output out_11,
  output out_12,
  output [3:0] out_13,
  output [31:0] out_14,
  output [31:0] out_15
);

  wire rst_n;

  Reset reset_1 (.out(rst_n));
  riscvmcu #(.applicationType("Socket")) u_riscvmcu (
    .clk(timeclk), .rst_n(rst_n), .clk_timer(timeclk), .digital_flash_data(in_3), .digital_mem_data(in_4),
    .digital_flash_addr(out_5), .digital_flash_write_en(out_6), .digital_flash_read_en(out_7),
    .digital_flash_byte_size(out_8), .digital_flash_wdata(out_9), .digital_mem_addr(out_10),
    .digital_mem_write_en(out_11), .digital_mem_read_en(out_12), .digital_mem_byte_size(out_13),
    .digital_mem_wdata(out_14), .gpio_values_out(out_15));

  // Other names for the same wires on the sheet: clk = C; clk_timer = timeclk

  // Notes on the sheet:
  //   C: Hz: 50
endmodule

/* Code of riscvmcu:
127.0.0.1:8009
*/
